# Fritzing sketch keybus_dscmod (saved by Fritzing 0.9.2b)

parts:
  Level_Shifter = Logic Level Converter
  Raspberry_Pi1 = Raspberry Pi B rev2

nets:
  N1: Level_Shifter.TX2_LV, Raspberry_Pi1.GPIO_7
  GND: Level_Shifter.GND, Raspberry_Pi1.GND
  N2: Level_Shifter.LV, Raspberry_Pi1.3V3
  N3: Level_Shifter.TX_LV, Raspberry_Pi1.GPIO_8

notes:
  Connect to DSC KeyBus
  DATA + - CLK
